// Logisim project decodificadores.circ as structural Verilog: 1 circuit, main circuit main
module main (
  input  in_1,
  input  Q7,
  input  Q6,
  input  Q5,
  input  Q4,
  input  Q3,
  input  Q2,
  input  Q1,
  input  Q0,
  input  in_10,
  input  in_11,
  input  in_12,
  input  in_13,
  input  in_14,
  input  in_15,
  input  in_16
);

  wire and_1_out, and_2_out, and_3_out, and_4_out, and_5_out, and_6_out, and_7_out, and_8_out, and_9_out,
       and_10_out, and_11_out, and_12_out, and_13_out, and_14_out, and_15_out, and_16_out,
       l_7448_bcd_to_7_seg_display_decoder_driver_common_cathode_22e8fb1e_1_p2,
       l_7448_bcd_to_7_seg_display_decoder_driver_common_cathode_22e8fb1e_1_p5,
       l_7448_bcd_to_7_seg_display_decoder_driver_common_cathode_22e8fb1e_1_p8,
       l_7448_bcd_to_7_seg_display_decoder_driver_common_cathode_22e8fb1e_1_p10,
       l_7448_bcd_to_7_seg_display_decoder_driver_common_cathode_22e8fb1e_1_p12, not_1_out, not_2_out,
       not_3_out, not_4_out, not_5_out, not_6_out, not_7_out, or_1_out, undriven, undriven_2, undriven_3,
       undriven_4, undriven_5, undriven_6, undriven_7, xor_1_out;

  not not_1 (not_1_out, Q6);
  not not_2 (not_2_out, Q3);
  not not_3 (not_3_out, Q2);
  not not_4 (not_4_out, Q4);
  not not_5 (not_5_out, Q2);
  not not_6 (not_6_out, Q1);
  not not_7 (not_7_out, Q0);
  and and_1 (and_1_out, Q7, not_1_out);
  and and_2 (and_2_out, Q5, Q4);
  and and_3 (and_3_out, not_2_out, not_3_out);
  and and_4 (and_4_out, Q1, Q0);
  and and_5 (and_5_out, Q7, Q6);
  and and_6 (and_6_out, Q5, not_4_out);
  and and_7 (and_7_out, Q3, not_5_out);
  and and_8 (and_8_out, not_6_out, not_7_out);
  and and_9 (and_9_out, and_1_out, and_2_out);
  and and_10 (and_10_out, and_3_out, and_4_out);
  and and_11 (and_11_out, and_5_out, and_6_out);
  and and_12 (and_12_out, and_7_out, and_8_out);
  and and_13 (and_13_out, and_9_out, and_10_out);
  and and_14 (and_14_out, and_11_out, and_12_out);
  LED led_1 (.in(and_13_out));
  LED led_2 (.in(and_14_out));
  or or_1 (or_1_out, and_13_out, and_14_out);
  and and_15 (and_15_out, and_13_out, or_1_out);
  and and_16 (and_16_out, or_1_out, and_14_out);
  // L_7448_BCD_to_7_Seg_Display_Decoder_Driver_Common_Cathode_22e8fb1e l_7448_bcd_to_7_seg_display_decoder_driver_common_cathode_22e8fb1e_1: pin names not known; wires that end beside it: and_16_out, l_7448_bcd_to_7_seg_display_decoder_driver_common_cathode_22e8fb1e_1_p2, in_16, in_15, l_7448_bcd_to_7_seg_display_decoder_driver_common_cathode_22e8fb1e_1_p5, in_15, in_16, l_7448_bcd_to_7_seg_display_decoder_driver_common_cathode_22e8fb1e_1_p8, and_15_out, l_7448_bcd_to_7_seg_display_decoder_driver_common_cathode_22e8fb1e_1_p10, in_16, l_7448_bcd_to_7_seg_display_decoder_driver_common_cathode_22e8fb1e_1_p12
  _7_Segment_Display #(.decimalPoint("false")) u_7_segment_display_1 (
    .g(l_7448_bcd_to_7_seg_display_decoder_driver_common_cathode_22e8fb1e_1_p2), .f(in_1),
    .a(l_7448_bcd_to_7_seg_display_decoder_driver_common_cathode_22e8fb1e_1_p5),
    .b(l_7448_bcd_to_7_seg_display_decoder_driver_common_cathode_22e8fb1e_1_p2),
    .e(l_7448_bcd_to_7_seg_display_decoder_driver_common_cathode_22e8fb1e_1_p12), .d(xor_1_out),
    .c(l_7448_bcd_to_7_seg_display_decoder_driver_common_cathode_22e8fb1e_1_p8));
  xor xor_1 (xor_1_out, l_7448_bcd_to_7_seg_display_decoder_driver_common_cathode_22e8fb1e_1_p10, and_15_out);
  _7_Segment_Display u_7_segment_display_2 (
    .g(undriven_2), .f(undriven), .a(undriven_3), .b(undriven_4), .e(undriven_5), .d(undriven_6),
    .c(undriven_7));  // open: dp

  // Notes on the sheet:
  //   Abierto
  //   Cerrado
endmodule
