// Logisim project serializador.circ as structural Verilog: 1 circuit, main circuit main
module main (
  input  in_1,
  input  in_2
);

  wire n74164_1_pin3, n74164_1_pin4, n74164_1_pin5, n74164_1_pin6, n74164_1_pin7, n74164_1_pin8,
       n74164_1_pin10, n74164_1_pin11, n74164_1_pin12, n74164_1_pin13;

  _74164 #(.ShowInternalStructure("true"), .VccGndPorts("true")) u_74164_1 (
    .pin1(in_2), .pin2(in_2), .pin3(n74164_1_pin3), .pin4(n74164_1_pin4), .pin5(n74164_1_pin5),
    .pin6(n74164_1_pin6), .pin7(n74164_1_pin7), .pin14(in_1), .pin13(n74164_1_pin13), .pin12(n74164_1_pin12),
    .pin11(n74164_1_pin11), .pin10(n74164_1_pin10), .pin8(n74164_1_pin8));  // open: pin9
  Clock clock_1 (.out(n74164_1_pin8));
  LED led_1 (.in(n74164_1_pin3));
  LED led_2 (.in(n74164_1_pin4));
  LED led_3 (.in(n74164_1_pin5));
  LED led_4 (.in(n74164_1_pin6));
  LED led_5 (.in(n74164_1_pin10));
  LED led_6 (.in(n74164_1_pin11));
  LED led_7 (.in(n74164_1_pin12));
  LED led_8 (.in(n74164_1_pin13));
  // also tied to GND on the sheet: n74164_1_pin7
endmodule
